// Logisim project CPU-LDSW.circ as structural Verilog: 15 circuits, main circuit main
module main (
  input  [5:0] in_1,
  output [31:0] out_2,
  output [3:0] out_3
);

  wire _1, _2, _3, _4, _5, _6, _7, _8, _9, AluOp0, AluOp1, ALUsrc, Branch, Check, CLK, EN, ENABLE, jump,
       Mem2Reg, MemRead, MemWrite, not_1_out, not_2_out, opcode_1_s0, opcode_1_s1, opcode_1_s2, opcode_1_s3,
       opcode_1_s4, opcode_1_s5, opcode_1_s6, opcode_2_s0, opcode_2_s1, opcode_2_s2, opcode_2_s3,
       opcode_2_s4, opcode_2_s5, opcode_2_s6, opcode_3_s0, opcode_3_s1, opcode_3_s2, opcode_3_s3,
       opcode_3_s4, opcode_3_s5, opcode_3_s6, opcode_4_s0, opcode_4_s1, opcode_4_s2, opcode_4_s3,
       opcode_4_s4, opcode_4_s5, opcode_4_s6, or_1_out, pipeline1_1_medreada, pipeline1_1_memreg2,
       pipeline1_1_memwrite2, pipeline1_1_regwritea, pipeline1_2_memreg2, pipeline1_2_regwritea,
       pipeline_2_aluop0a, pipeline_2_aluop1a, pipeline_2_alusrca, pipeline_2_medreada, pipeline_2_memreg2,
       pipeline_2_memwrite2, pipeline_2_regwritea, regDst, RegWrite, Resetti, S, zero;
  wire [1:0] haz_1_out_8, haz_1_out_9;
  wire [4:0] multiplexer_6_out, pipeline1_1_rda, pipeline1_1_regdesta_2, pipeline1_1_rsa, pipeline1_1_rta,
       pipeline1_2_regdesta_2, pipeline_1_rda, pipeline_1_rsa, pipeline_1_rta, pipeline_1_shamta,
       pipeline_2_rda, pipeline_2_rsa, pipeline_2_rta, Rd, RS, RT, shamt;
  wire [5:0] decoder_1_op, FUNC, FUNCT, FUNCx, OP, OPx, pipeline1_1_functa, pipeline1_1_opa,
       pipeline_2_functa, pipeline_2_opa;
  wire [14:0] multiplexer_1_out;
  wire [15:0] Imm, pipeline_1_imma, pipeline_2_imma;
  wire [23:0] bit_extender_1_out, PC1, pc_change_1_pc_out, pcX, pipeline1_1_pca, pipeline_2_pca, Xpc;
  wire [25:0] targetJump;
  wire [31:0] Address, multiplexer_7_out, multiplexer_8_out, multiplexer_10_out, pipeline1_1_alurega,
       pipeline1_1_busba, pipeline1_2_alurega, pipeline1_2_xa, pipeline_2_busaa, pipeline_2_busba,
       ram_1_data, RegA, register_file_1_res_reg_b, validateaddi_1_rb;

  Register #(.width(24)) register_1 (.D(pc_change_1_pc_out), .en(EN), .Q(PC1), .clk(CLK), .clr(Resetti));
  Button button_1 (.out(Resetti));
  // Probe on PC1
  ROM #(.addrWidth(24), .dataWidth(32)) rom_1 (.addr(PC1), .data(Address));  // open: sel
  PC_Change pc_change_1 (
    .PC(PC1), .Target_Jump(targetJump), .PC_Out(pc_change_1_pc_out), .Jump_Control(jump), .Offset(Imm),
    .Branch(Branch), .Zero(zero));
  Opcode opcode_1 (
    .F0(FUNCT[0]), .F1(FUNCT[1]), .F2(FUNCT[2]), .F3(FUNCT[3]), .F4(FUNCT[4]), .F5(FUNCT[5]),
    .OP0(decoder_1_op[0]), .OP1(decoder_1_op[1]), .OP2(decoder_1_op[2]), .OP3(decoder_1_op[3]),
    .OP4(decoder_1_op[4]), .OP5(decoder_1_op[5]), .S0(opcode_1_s0), .S1(opcode_1_s1), .S2(opcode_1_s2),
    .S3(opcode_1_s3), .S4(opcode_1_s4), .S5(opcode_1_s5), .S6(opcode_1_s6));
  Decoder decoder_1 (
    .Instruction(Address), .Target_Jump(targetJump), .Fucnt(FUNCT), .Shamt(shamt), .Rd(Rd), .Immediate(Imm),
    .Rt(RT), .Rs(RS), .Op(decoder_1_op));
  _7_Segment_Display u_7_segment_display_1 (
    .g(opcode_1_s6), .f(opcode_1_s5), .a(opcode_1_s0), .b(opcode_1_s1), .e(opcode_1_s4), .d(opcode_1_s3),
    .c(opcode_1_s2));  // open: dp
  not not_1 (not_1_out, S);
  PIPELINE pipeline_1 (
    .OP(decoder_1_op), .RS(RS), .RT(RT), .RD(Rd), .IMM(Imm), .SHAMT(shamt), .FUNCT(FUNCT), .PC(PC1),
    .ENABLE(not_1_out), .RELOJ(CLK), .RESET(Resetti), .OPA(OP), .RSA(pipeline_1_rsa), .RTA(pipeline_1_rta),
    .RDA(pipeline_1_rda), .IMMA(pipeline_1_imma), .SHAMTA(pipeline_1_shamta), .FUNCTA(FUNC), .PCA(pcX));  // open: RegDest, AluSrc, Mem2Reg, RegWrite, MemRead, MemWrite, Branch, AluOp1, AluOp0, Jump, MemReg, BusA, BusB, AluReg, RegDest_2, X, RegDestA, AluSrcA, MemReg2, RegWriteA, MedReadA, MemWrite2, BranchA, AluOp1A, AluOp0A, JumpA, MemRegA, BusAA, BusBA, AluRegA, RegDestA_2, XA
  // Probe on pipeline_1_rta
  // Probe on pipeline_1_rsa
  // Probe on pipeline_1_rda
  control_unit control_unit_1 (
    .op5(OP[5]), .op4(OP[4]), .regDst(regDst), .op3(OP[3]), .op2(OP[2]), .op1(OP[1]), .op0(OP[0]),
    .aluSrc(ALUsrc), .memToReg(Mem2Reg), .regWrite(RegWrite), .memRead(MemRead), .memWrite(MemWrite),
    .branch(Branch), .aluOp1(AluOp1), .aluOp0(AluOp0), .jump(jump));
  Multiplexer #(.width(15)) multiplexer_1 (
    .in0({pipeline_1_rda, pipeline_1_rta, pipeline_1_rsa}), .in1({15{1'b0}}), .out(multiplexer_1_out), .sel(S));  // open: en
  Opcode opcode_2 (
    .F0(FUNC[0]), .F1(FUNC[1]), .F2(FUNC[2]), .F3(FUNC[3]), .F4(FUNC[4]), .F5(FUNC[5]), .OP0(OP[0]),
    .OP1(OP[1]), .OP2(OP[2]), .OP3(OP[3]), .OP4(OP[4]), .OP5(OP[5]), .S0(opcode_2_s0), .S1(opcode_2_s1),
    .S2(opcode_2_s2), .S3(opcode_2_s3), .S4(opcode_2_s4), .S5(opcode_2_s5), .S6(opcode_2_s6));
  not not_2 (not_2_out, CLK);
  _7_Segment_Display u_7_segment_display_2 (
    .g(opcode_2_s6), .f(opcode_2_s5), .a(opcode_2_s0), .b(opcode_2_s1), .e(opcode_2_s4), .d(opcode_2_s3),
    .c(opcode_2_s2));  // open: dp
  Multiplexer #(.width(9)) multiplexer_2 (
    .in0({AluOp0, AluOp1, Branch, MemWrite, MemRead, RegWrite, Mem2Reg, ALUsrc, regDst}), .in1({9{1'b0}}),
    .out({_9, _8, _7, _6, _5, _4, _3, _2, _1}), .sel(S));  // open: en
  Multiplexer #(.width(24)) multiplexer_3 (.in0(pcX), .in1({24{1'b0}}), .out(Xpc), .sel(S));  // open: en
  Multiplexer #(.width(6)) multiplexer_4 (.in0(OP), .in1({6{1'b0}}), .out(OPx), .sel(S));  // open: en
  Register_File register_file_1 (
    .Data_In(multiplexer_10_out), .Write_Enable(pipeline1_2_regwritea), .Res_Reg_A(RegA),
    .Res_Reg_B(register_file_1_res_reg_b), .Registro_C(pipeline1_2_regdesta_2), .Registro_A(pipeline_1_rsa),
    .Registro_B(pipeline_1_rta), .CLK(not_2_out), .Reset(Resetti));
  // Probe on pcX
  Multiplexer #(.width(6)) multiplexer_5 (.in0(FUNC), .in1(6'b011000), .out(FUNCx), .sel(S));  // open: en
  HazardUnitLS hazardunitls_1 (
    .ID_EX_MemRead(pipeline_2_medreada), .ID_EX_RegisterRT(pipeline_2_rta),
    .IF_ID_RegisterRS(pipeline_1_rsa), .IF_ID_RegisterRT(pipeline_1_rta), .out_5(S));
  PIPELINE pipeline_2 (
    .OP(OPx), .RS(multiplexer_1_out[4:0]), .RT(multiplexer_1_out[9:5]), .RD(multiplexer_1_out[14:10]),
    .IMM(pipeline_1_imma), .SHAMT(pipeline_1_shamta), .FUNCT(FUNCx), .RegDest(_1), .AluSrc(_2), .Mem2Reg(_3),
    .RegWrite(_4), .MemRead(_5), .MemWrite(_6), .Branch(_7), .AluOp1(_8), .AluOp0(_9), .Jump(jump),
    .BusA(RegA), .BusB(register_file_1_res_reg_b), .PC(Xpc), .ENABLE(EN), .RELOJ(CLK), .RESET(Resetti),
    .OPA(pipeline_2_opa), .RSA(pipeline_2_rsa), .RTA(pipeline_2_rta), .RDA(pipeline_2_rda),
    .IMMA(pipeline_2_imma), .FUNCTA(pipeline_2_functa), .AluSrcA(pipeline_2_alusrca),
    .MemReg2(pipeline_2_memreg2), .RegWriteA(pipeline_2_regwritea), .MedReadA(pipeline_2_medreada),
    .MemWrite2(pipeline_2_memwrite2), .AluOp1A(pipeline_2_aluop1a), .AluOp0A(pipeline_2_aluop0a),
    .BusAA(pipeline_2_busaa), .BusBA(pipeline_2_busba), .PCA(pipeline_2_pca));  // open: MemReg, AluReg, RegDest_2, X, SHAMTA, RegDestA, BranchA, JumpA, MemRegA, AluRegA, RegDestA_2, XA
  // Probe on pipeline_2_functa
  // Probe on pipeline_2_opa
  Multiplexer #(.width(5), .enable("false")) multiplexer_6 (
    .in0(pipeline_2_rda), .in1(pipeline_2_rta), .out(multiplexer_6_out), .sel(pipeline_2_alusrca));
  HAZ haz_1 (
    .RD__0(pipeline1_1_regdesta_2), .RegWrite__1(pipeline1_1_regwritea), .in_2(pipeline1_2_regwritea),
    .in_1(pipeline1_2_regdesta_2), .out_7(ENABLE), .in_5(pipeline_2_rsa), .RD__RT(pipeline_2_rta),
    .out_8(haz_1_out_8), .out_9(haz_1_out_9));
  // Probe on haz_1_out_9
  // Probe on haz_1_out_8
  Multiplexer #(.select(2), .width(32)) multiplexer_7 (
    .in0(pipeline_2_busaa), .in1(multiplexer_10_out), .in2(pipeline1_1_alurega), .out(multiplexer_7_out),
    .sel(haz_1_out_8));  // open: in3, en
  Multiplexer #(.select(2), .width(32)) multiplexer_8 (
    .in0(pipeline_2_busba), .in1(multiplexer_10_out), .in2(pipeline1_1_alurega), .out(multiplexer_8_out),
    .sel(haz_1_out_9));  // open: in3, en
  Opcode opcode_3 (
    .F0(pipeline_2_functa[0]), .F1(pipeline_2_functa[1]), .F2(pipeline_2_functa[2]),
    .F3(pipeline_2_functa[3]), .F4(pipeline_2_functa[4]), .F5(pipeline_2_functa[5]), .OP0(pipeline_2_opa[0]),
    .OP1(pipeline_2_opa[1]), .OP2(pipeline_2_opa[2]), .OP3(pipeline_2_opa[3]), .OP4(pipeline_2_opa[4]),
    .OP5(pipeline_2_opa[5]), .S0(opcode_3_s0), .S1(opcode_3_s1), .S2(opcode_3_s2), .S3(opcode_3_s3),
    .S4(opcode_3_s4), .S5(opcode_3_s5), .S6(opcode_3_s6));
  ALU alu_1 (.A(multiplexer_7_out), .B(validateaddi_1_rb), .R(out_2), .operation(out_3), .zero(zero));
  ValidateAddi validateaddi_1 (
    .Rt(multiplexer_8_out), .Imm(pipeline_2_imma), .Rb(validateaddi_1_rb), .ALUSrc(pipeline_2_alusrca));
  control_sign_ALU control_sign_alu_1 (
    .aluOp1(pipeline_2_aluop1a), .aluOp0(pipeline_2_aluop0a), .f5(pipeline_2_functa[5]),
    .f4(pipeline_2_functa[4]), .f3(pipeline_2_functa[3]), .f2(pipeline_2_functa[2]),
    .f1(pipeline_2_functa[1]), .oper3(out_3[3]), .f0(pipeline_2_functa[0]), .oper2(out_3[2]),
    .oper1(out_3[1]), .oper0(out_3[0]));
  not not_3 (Check, ENABLE);
  Multiplexer multiplexer_9 (.in0(Check), .in1(ENABLE), .out(EN), .sel(ENABLE));  // open: en
  _7_Segment_Display u_7_segment_display_3 (
    .g(opcode_3_s6), .f(opcode_3_s5), .a(opcode_3_s0), .b(opcode_3_s1), .e(opcode_3_s4), .d(opcode_3_s3),
    .c(opcode_3_s2));  // open: dp
  // Probe on pipeline_2_pca
  Clock clock_1 (.out(CLK));
  PIPELINE1 pipeline1_1 (
    .OP(pipeline_2_opa), .RS(pipeline_2_rsa), .RT(pipeline_2_rta), .RD(pipeline_2_rda),
    .FUNCT(pipeline_2_functa), .AluSrc(pipeline_2_alusrca), .Mem2Reg(pipeline_2_memreg2),
    .RegWrite(pipeline_2_regwritea), .MemRead(pipeline_2_medreada), .MemWrite(pipeline_2_memwrite2),
    .BusB(multiplexer_8_out), .AluReg(out_2), .RegDest_2(multiplexer_6_out), .PC(pipeline_2_pca),
    .ENABLE(EN), .RELOJ(CLK), .RESET(Resetti), .OPA(pipeline1_1_opa), .RSA(pipeline1_1_rsa),
    .RTA(pipeline1_1_rta), .RDA(pipeline1_1_rda), .FUNCTA(pipeline1_1_functa), .MemReg2(pipeline1_1_memreg2),
    .RegWriteA(pipeline1_1_regwritea), .MedReadA(pipeline1_1_medreada), .MemWrite2(pipeline1_1_memwrite2),
    .BusBA(pipeline1_1_busba), .AluRegA(pipeline1_1_alurega), .RegDestA_2(pipeline1_1_regdesta_2),
    .PCA(pipeline1_1_pca));  // open: IMM, SHAMT, RegDest, Branch, AluOp1, AluOp0, Jump, MemReg, BusA, X, IMMA, SHAMTA, RegDestA, AluSrcA, BranchA, AluOp1A, AluOp0A, JumpA, MemRegA, BusAA, XA
  Bit_Extender #(.in_width(32), .out_width(24)) bit_extender_1 (.in(pipeline1_1_alurega), .out(bit_extender_1_out));
  or or_1 (or_1_out, pipeline1_1_memwrite2, pipeline1_1_medreada);
  _7_Segment_Display u_7_segment_display_4 (
    .g(opcode_4_s6), .f(opcode_4_s5), .a(opcode_4_s0), .b(opcode_4_s1), .e(opcode_4_s4), .d(opcode_4_s3),
    .c(opcode_4_s2));  // open: dp
  Opcode opcode_4 (
    .F0(pipeline1_1_functa[0]), .F1(pipeline1_1_functa[1]), .F2(pipeline1_1_functa[2]),
    .F3(pipeline1_1_functa[3]), .F4(pipeline1_1_functa[4]), .F5(pipeline1_1_functa[5]),
    .OP0(pipeline1_1_opa[0]), .OP1(pipeline1_1_opa[1]), .OP2(pipeline1_1_opa[2]), .OP3(pipeline1_1_opa[3]),
    .OP4(pipeline1_1_opa[4]), .OP5(pipeline1_1_opa[5]), .S0(opcode_4_s0), .S1(opcode_4_s1), .S2(opcode_4_s2),
    .S3(opcode_4_s3), .S4(opcode_4_s4), .S5(opcode_4_s5), .S6(opcode_4_s6));
  RAM #(.addrWidth(24), .dataWidth(32), .bus("separate")) ram_1 (
    .addr(bit_extender_1_out), .din(pipeline1_1_busba), .data(ram_1_data), .sel(or_1_out), .clk(CLK),
    .ld(pipeline1_1_medreada), .clr(Resetti));  // open: str
  // Probe on pipeline1_1_pca
  PIPELINE1 pipeline1_2 (
    .RS(pipeline1_1_rsa), .RT(pipeline1_1_rta), .RD(pipeline1_1_rda), .Mem2Reg(pipeline1_1_memreg2),
    .RegWrite(pipeline1_1_regwritea), .MemRead(pipeline1_1_medreada), .AluReg(pipeline1_1_alurega),
    .RegDest_2(pipeline1_1_regdesta_2), .X(ram_1_data), .PC(pipeline1_1_pca), .ENABLE(EN), .RELOJ(CLK),
    .RESET(Resetti), .MemReg2(pipeline1_2_memreg2), .RegWriteA(pipeline1_2_regwritea),
    .AluRegA(pipeline1_2_alurega), .RegDestA_2(pipeline1_2_regdesta_2), .XA(pipeline1_2_xa));  // open: OP, IMM, SHAMT, FUNCT, RegDest, AluSrc, MemWrite, Branch, AluOp1, AluOp0, Jump, MemReg, BusA, BusB, OPA, RSA, RTA, RDA, IMMA, SHAMTA, FUNCTA, RegDestA, AluSrcA, MedReadA, MemWrite2, BranchA, AluOp1A, AluOp0A, JumpA, MemRegA, BusAA, BusBA, PCA
  Multiplexer #(.width(32), .enable("false")) multiplexer_10 (
    .in0(pipeline1_2_alurega), .in1(pipeline1_2_xa), .out(multiplexer_10_out), .sel(pipeline1_2_memreg2));

  // Other names for the same wires on the sheet: MemAdd[31:0] = out_2

  // Notes on the sheet:
  //    PC
  //   contents of rom_1 (hex, n*v repeats v):
  //   21080001 21290001 1294020 1084820 5*218c0001 ad490000 6*218c0001 8d4b0000 16b5820
  //    7-Segmentos no mostrará valores para instrucción ADDi
  //   d: ADDI
  //   A: ADD
  //   S:SUB
  //   r:STORE
  //   L:LOAD
  //    E: STALL
  //    STAGE ID
  //   Control Unit 
  //    PC
  //   d: ADDI
  //   A: ADD
  //   S:SUB
  //   r:STORE
  //   L:LOAD
  //    E: STALL
  //    STAGE REG
  //    ALU Control
  //   d: ADDI
  //   A: ADD
  //   S:SUB
  //   r:STORE
  //   L:LOAD
  //    E: STALL
  //    7-Segmentos no mostrará valores para instrucción ADDi
  //    PC
  //    PC
  //   d: ADDI
  //   A: ADD
  //   S:SUB
  //   r:STORE
  //   L:LOAD
  //    E: STALL
  //    7-Segmentos no mostrará valores para instrucción ADDi
endmodule

module Decoder (
  input  [31:0] Instruction,
  output [25:0] Target_Jump,
  output [5:0] Fucnt,
  output [4:0] Shamt,
  output [4:0] Rd,
  output [15:0] Immediate,
  output [4:0] Rt,
  output [4:0] Rs,
  output [5:0] Op
);


  assign Fucnt = Instruction[5:0];
  assign Immediate = Instruction[15:0];
  assign Op = Instruction[31:26];
  assign Rd = Instruction[15:11];
  assign Rs = Instruction[25:21];
  assign Rt = Instruction[20:16];
  assign Shamt = Instruction[10:6];
  assign Target_Jump = Instruction[25:0];
endmodule

module Register_File (
  input  [31:0] Data_In,
  input  Reset,
  input  Write_Enable,
  input  [4:0] Registro_A,
  input  [4:0] Registro_C,
  input  [4:0] Registro_B,
  input  CLK,
  output [31:0] Res_Reg_A,
  output [31:0] Res_Reg_B
);

  wire and_1_out, and_2_out, and_3_out, and_4_out, and_5_out, and_6_out, and_7_out, and_8_out, and_9_out,
       and_10_out, and_11_out, and_12_out, and_13_out, and_14_out, and_15_out, and_16_out, and_17_out,
       and_18_out, and_19_out, and_20_out, and_21_out, and_22_out, and_23_out, and_24_out, and_25_out,
       and_26_out, and_27_out, and_28_out, and_29_out, and_30_out, and_31_out, and_32_out, decoder_1_out0,
       decoder_1_out1, decoder_1_out2, decoder_1_out3, decoder_1_out4, decoder_1_out5, decoder_1_out6,
       decoder_1_out7, decoder_1_out8, decoder_1_out9, decoder_1_out10, decoder_1_out11, decoder_1_out12,
       decoder_1_out13, decoder_1_out14, decoder_1_out15, decoder_1_out16, decoder_1_out17, decoder_1_out18,
       decoder_1_out19, decoder_1_out20, decoder_1_out21, decoder_1_out22, decoder_1_out23, decoder_1_out24,
       decoder_1_out25, decoder_1_out26, decoder_1_out27, decoder_1_out28, decoder_1_out29, decoder_1_out30,
       decoder_1_out31;
  wire [31:0] register_1_q, register_2_q, register_3_q, register_4_q, register_5_q, register_6_q,
       register_7_q, register_8_q, register_9_q, register_10_q, register_11_q, register_12_q, register_13_q,
       register_14_q, register_15_q, register_16_q, register_17_q, register_18_q, register_19_q,
       register_20_q, register_21_q, register_22_q, register_23_q, register_24_q, register_25_q,
       register_26_q, register_27_q, register_28_q, register_29_q, register_30_q, register_31_q,
       register_32_q;

  Decoder_part #(.select(5), .enable("false")) decoder_1 (
    .out0(decoder_1_out0), .out1(decoder_1_out1), .out2(decoder_1_out2), .out3(decoder_1_out3),
    .out4(decoder_1_out4), .out5(decoder_1_out5), .out6(decoder_1_out6), .out7(decoder_1_out7),
    .out8(decoder_1_out8), .out9(decoder_1_out9), .out10(decoder_1_out10), .out11(decoder_1_out11),
    .out12(decoder_1_out12), .out13(decoder_1_out13), .out14(decoder_1_out14), .out15(decoder_1_out15),
    .out16(decoder_1_out16), .out17(decoder_1_out17), .out18(decoder_1_out18), .out19(decoder_1_out19),
    .out20(decoder_1_out20), .out21(decoder_1_out21), .out22(decoder_1_out22), .out23(decoder_1_out23),
    .out24(decoder_1_out24), .out25(decoder_1_out25), .out26(decoder_1_out26), .out27(decoder_1_out27),
    .out28(decoder_1_out28), .out29(decoder_1_out29), .out30(decoder_1_out30), .out31(decoder_1_out31),
    .sel(Registro_C));
  and and_1 (and_1_out, Write_Enable, decoder_1_out0);
  and and_2 (and_2_out, Write_Enable, decoder_1_out1);
  and and_3 (and_3_out, Write_Enable, decoder_1_out2);
  and and_4 (and_4_out, Write_Enable, decoder_1_out3);
  and and_5 (and_5_out, Write_Enable, decoder_1_out4);
  and and_6 (and_6_out, Write_Enable, decoder_1_out5);
  and and_7 (and_7_out, Write_Enable, decoder_1_out6);
  and and_8 (and_8_out, Write_Enable, decoder_1_out7);
  Register #(.width(32)) register_1 (.D(Data_In), .en(and_1_out), .Q(register_1_q), .clk(CLK), .clr(Reset));
  Register #(.width(32)) register_2 (.D(Data_In), .en(and_2_out), .Q(register_2_q), .clk(CLK), .clr(Reset));
  Register #(.width(32)) register_3 (.D(Data_In), .en(and_3_out), .Q(register_3_q), .clk(CLK), .clr(Reset));
  Register #(.width(32)) register_4 (.D(Data_In), .en(and_4_out), .Q(register_4_q), .clk(CLK), .clr(Reset));
  Register #(.width(32)) register_5 (.D(Data_In), .en(and_5_out), .Q(register_5_q), .clk(CLK), .clr(Reset));
  Register #(.width(32)) register_6 (.D(Data_In), .en(and_6_out), .Q(register_6_q), .clk(CLK), .clr(Reset));
  Register #(.width(32)) register_7 (.D(Data_In), .en(and_7_out), .Q(register_7_q), .clk(CLK), .clr(Reset));
  Register #(.width(32)) register_8 (.D(Data_In), .en(and_8_out), .Q(register_8_q), .clk(CLK), .clr(Reset));
  and and_9 (and_9_out, Write_Enable, decoder_1_out8);
  Register #(.width(32)) register_9 (.D(Data_In), .en(and_9_out), .Q(register_9_q), .clk(CLK), .clr(Reset));
  Register #(.width(32)) register_10 (.D(Data_In), .en(and_10_out), .Q(register_10_q), .clk(CLK), .clr(Reset));
  and and_10 (and_10_out, Write_Enable, decoder_1_out9);
  and and_11 (and_11_out, Write_Enable, decoder_1_out10);
  Register #(.width(32)) register_11 (.D(Data_In), .en(and_11_out), .Q(register_11_q), .clk(CLK), .clr(Reset));
  and and_12 (and_12_out, Write_Enable, decoder_1_out11);
  Register #(.width(32)) register_12 (.D(Data_In), .en(and_12_out), .Q(register_12_q), .clk(CLK), .clr(Reset));
  Register #(.width(32)) register_13 (.D(Data_In), .en(and_13_out), .Q(register_13_q), .clk(CLK), .clr(Reset));
  and and_13 (and_13_out, Write_Enable, decoder_1_out12);
  Register #(.width(32)) register_14 (.D(Data_In), .en(and_14_out), .Q(register_14_q), .clk(CLK), .clr(Reset));
  and and_14 (and_14_out, Write_Enable, decoder_1_out13);
  and and_15 (and_15_out, Write_Enable, decoder_1_out14);
  Register #(.width(32)) register_15 (.D(Data_In), .en(and_15_out), .Q(register_15_q), .clk(CLK), .clr(Reset));
  Register #(.width(32)) register_16 (.D(Data_In), .en(and_16_out), .Q(register_16_q), .clk(CLK), .clr(Reset));
  and and_16 (and_16_out, Write_Enable, decoder_1_out15);
  and and_17 (and_17_out, Write_Enable, decoder_1_out16);
  and and_18 (and_18_out, Write_Enable, decoder_1_out17);
  and and_19 (and_19_out, Write_Enable, decoder_1_out18);
  and and_20 (and_20_out, Write_Enable, decoder_1_out19);
  and and_21 (and_21_out, Write_Enable, decoder_1_out20);
  and and_22 (and_22_out, Write_Enable, decoder_1_out21);
  and and_23 (and_23_out, Write_Enable, decoder_1_out22);
  and and_24 (and_24_out, Write_Enable, decoder_1_out23);
  Register #(.width(32)) register_17 (.D(Data_In), .en(and_17_out), .Q(register_17_q), .clk(CLK), .clr(Reset));
  Register #(.width(32)) register_18 (.D(Data_In), .en(and_18_out), .Q(register_18_q), .clk(CLK), .clr(Reset));
  Register #(.width(32)) register_19 (.D(Data_In), .en(and_19_out), .Q(register_19_q), .clk(CLK), .clr(Reset));
  Register #(.width(32)) register_20 (.D(Data_In), .en(and_20_out), .Q(register_20_q), .clk(CLK), .clr(Reset));
  Register #(.width(32)) register_21 (.D(Data_In), .en(and_21_out), .Q(register_21_q), .clk(CLK), .clr(Reset));
  Register #(.width(32)) register_22 (.D(Data_In), .en(and_22_out), .Q(register_22_q), .clk(CLK), .clr(Reset));
  Register #(.width(32)) register_23 (.D(Data_In), .en(and_23_out), .Q(register_23_q), .clk(CLK), .clr(Reset));
  Register #(.width(32)) register_24 (.D(Data_In), .en(and_24_out), .Q(register_24_q), .clk(CLK), .clr(Reset));
  and and_25 (and_25_out, Write_Enable, decoder_1_out24);
  and and_26 (and_26_out, Write_Enable, decoder_1_out25);
  and and_27 (and_27_out, Write_Enable, decoder_1_out26);
  and and_28 (and_28_out, Write_Enable, decoder_1_out27);
  and and_29 (and_29_out, Write_Enable, decoder_1_out28);
  and and_30 (and_30_out, Write_Enable, decoder_1_out29);
  and and_31 (and_31_out, Write_Enable, decoder_1_out30);
  and and_32 (and_32_out, Write_Enable, decoder_1_out31);
  Register #(.width(32)) register_25 (.D(Data_In), .en(and_25_out), .Q(register_25_q), .clk(CLK), .clr(Reset));
  Register #(.width(32)) register_26 (.D(Data_In), .en(and_26_out), .Q(register_26_q), .clk(CLK), .clr(Reset));
  Register #(.width(32)) register_27 (.D(Data_In), .en(and_27_out), .Q(register_27_q), .clk(CLK), .clr(Reset));
  Register #(.width(32)) register_28 (.D(Data_In), .en(and_28_out), .Q(register_28_q), .clk(CLK), .clr(Reset));
  Register #(.width(32)) register_29 (.D(Data_In), .en(and_29_out), .Q(register_29_q), .clk(CLK), .clr(Reset));
  Register #(.width(32)) register_30 (.D(Data_In), .en(and_30_out), .Q(register_30_q), .clk(CLK), .clr(Reset));
  Register #(.width(32)) register_31 (.D(Data_In), .en(and_31_out), .Q(register_31_q), .clk(CLK), .clr(Reset));
  Register #(.width(32)) register_32 (.D(Data_In), .en(and_32_out), .Q(register_32_q), .clk(CLK));  // open: clr
  Multiplexer #(.select(5), .width(32), .enable("false")) multiplexer_1 (
    .in0(register_1_q), .in1(register_2_q), .in2(register_3_q), .in3(register_4_q), .in4(register_5_q),
    .in5(register_6_q), .in6(register_7_q), .in7(register_8_q), .in8(register_9_q), .in9(register_10_q),
    .in10(register_11_q), .in11(register_12_q), .in12(register_13_q), .in13(register_14_q),
    .in14(register_15_q), .in15(register_16_q), .in16(register_17_q), .in17(register_18_q),
    .in18(register_19_q), .in19(register_20_q), .in20(register_21_q), .in21(register_22_q),
    .in22(register_23_q), .in23(register_24_q), .in24(register_25_q), .in25(register_26_q),
    .in26(register_27_q), .in27(register_28_q), .in28(register_29_q), .in29(register_30_q),
    .in30(register_31_q), .in31(register_32_q), .out(Res_Reg_A), .sel(Registro_A));
  Multiplexer #(.select(5), .width(32), .enable("false")) multiplexer_2 (
    .in0(register_1_q), .in1(register_2_q), .in2(register_3_q), .in3(register_4_q), .in4(register_5_q),
    .in5(register_6_q), .in6(register_7_q), .in7(register_8_q), .in8(register_9_q), .in9(register_10_q),
    .in10(register_11_q), .in11(register_12_q), .in12(register_13_q), .in13(register_14_q),
    .in14(register_15_q), .in15(register_16_q), .in16(register_17_q), .in17(register_18_q),
    .in18(register_19_q), .in19(register_20_q), .in20(register_21_q), .in21(register_22_q),
    .in22(register_23_q), .in23(register_24_q), .in24(register_25_q), .in25(register_26_q),
    .in26(register_27_q), .in27(register_28_q), .in28(register_29_q), .in29(register_30_q),
    .in30(register_31_q), .in31(register_32_q), .out(Res_Reg_B), .sel(Registro_B));
endmodule

module Data_Hex (
  input  [31:0] Data,
  output [3:0] Digit_7,
  output [3:0] Digit_6,
  output [3:0] Digit_5,
  output [3:0] Digit_4,
  output [3:0] Digit_3,
  output [3:0] Digit_2,
  output [3:0] Digit_1,
  output [3:0] Digit_0
);


  assign Digit_0 = Data[3:0];
  assign Digit_1 = Data[7:4];
  assign Digit_2 = Data[11:8];
  assign Digit_3 = Data[15:12];
  assign Digit_4 = Data[19:16];
  assign Digit_5 = Data[23:20];
  assign Digit_6 = Data[27:24];
  assign Digit_7 = Data[31:28];
endmodule

module Opcode (
  input  F0,
  input  F1,
  input  F2,
  input  F3,
  input  F4,
  input  F5,
  input  OP0,
  input  OP1,
  input  OP2,
  input  OP3,
  input  OP4,
  input  OP5,
  output S0,
  output S1,
  output S2,
  output S3,
  output S4,
  output S5,
  output S6
);

  wire and_1_out, and_2_out, and_3_out, and_4_out, and_5_out, and_6_out, and_7_out, and_8_out, and_9_out,
       and_10_out, and_11_out, and_12_out, and_13_out, and_14_out, and_15_out, and_16_out, and_17_out,
       and_18_out, and_19_out, and_20_out, and_21_out, and_22_out, and_23_out, and_24_out, and_25_out,
       and_26_out, and_27_out, and_28_out, and_29_out, and_30_out, and_31_out, and_32_out, and_33_out,
       and_34_out, and_35_out, and_36_out, comparator_1_eq, comparator_2_eq, multiplexer_1_out,
       multiplexer_2_out, not_1_out, not_2_out, not_3_out, not_4_out, not_5_out, not_6_out, not_7_out,
       not_8_out, not_9_out, not_10_out, not_11_out, not_12_out, not_13_out, not_14_out, not_15_out,
       not_16_out, not_17_out, not_18_out, not_19_out, not_20_out, not_21_out, not_22_out, not_23_out,
       not_24_out, not_25_out, not_26_out, not_27_out, not_28_out, not_29_out, not_30_out, not_31_out,
       not_32_out, not_33_out, not_34_out, not_35_out, not_36_out, not_37_out, not_38_out, not_39_out,
       not_40_out, not_41_out, not_42_out, not_43_out, not_44_out, not_45_out, not_46_out, not_47_out,
       not_48_out, not_49_out, not_50_out, not_51_out, not_52_out, not_53_out, not_54_out, not_55_out,
       not_56_out, not_57_out, not_58_out, not_59_out, not_60_out, not_61_out, not_62_out, not_63_out,
       not_64_out, not_65_out, not_66_out, not_67_out, not_68_out, not_69_out, not_70_out, not_71_out,
       not_72_out, not_73_out, not_74_out, not_75_out, not_76_out, not_77_out, not_78_out, not_79_out,
       not_80_out, not_81_out, not_82_out, not_83_out, not_84_out, not_85_out, not_86_out, not_87_out,
       not_88_out, not_89_out, not_90_out, not_91_out, not_92_out, not_93_out, not_94_out, not_95_out,
       not_96_out, not_97_out, not_98_out, not_99_out, not_100_out, not_101_out, not_102_out, not_103_out,
       not_104_out, not_105_out, not_106_out, not_107_out, not_108_out, not_109_out, not_110_out,
       not_111_out, not_112_out, not_113_out, not_114_out, not_115_out, not_116_out, not_117_out,
       not_118_out, not_119_out, not_120_out, not_121_out, not_122_out, not_123_out, not_124_out,
       not_125_out, not_126_out, not_127_out, not_128_out, not_129_out, not_130_out, not_131_out,
       not_132_out, not_133_out, not_134_out, not_135_out, not_136_out, not_137_out, not_138_out,
       not_139_out, not_140_out, not_141_out, not_142_out, not_143_out, not_144_out, not_145_out,
       not_146_out, not_147_out, not_148_out, not_149_out, not_150_out, not_151_out, not_152_out,
       not_153_out, not_154_out, not_155_out, not_156_out, not_157_out, not_158_out, not_159_out,
       not_160_out, not_161_out, not_162_out, not_163_out, not_164_out, not_165_out, not_166_out,
       not_167_out, not_168_out, not_169_out, not_170_out, not_171_out, not_172_out, not_173_out,
       not_174_out, not_175_out, not_176_out, not_177_out, not_178_out, not_179_out, not_180_out,
       not_181_out, not_182_out, not_183_out, not_184_out, not_185_out, not_186_out, not_187_out,
       not_188_out, not_189_out, not_190_out, not_191_out, not_192_out, not_193_out, not_194_out,
       not_195_out, not_196_out, not_197_out, not_198_out, not_199_out, not_200_out, not_201_out,
       not_202_out, not_203_out, not_204_out, not_205_out, not_206_out, not_207_out, not_208_out,
       not_209_out, not_210_out, not_211_out, not_212_out, not_213_out, not_214_out, not_215_out,
       not_216_out, not_217_out, not_218_out, not_219_out, not_220_out, not_221_out, not_222_out,
       not_223_out, not_224_out, not_225_out, not_226_out, not_227_out, not_228_out, not_229_out,
       not_230_out, not_231_out, not_232_out, not_233_out, not_234_out, not_235_out, not_236_out,
       not_237_out, not_238_out, not_239_out, not_240_out, not_241_out, not_242_out, not_243_out,
       not_244_out, not_245_out, not_246_out, not_247_out, not_248_out, not_249_out, not_250_out,
       not_251_out, not_252_out, not_253_out, not_254_out, not_255_out, not_256_out, not_257_out,
       not_258_out, not_259_out, not_260_out, not_261_out, not_262_out, not_263_out, not_264_out,
       not_265_out, not_266_out, not_267_out, not_268_out, not_269_out, not_270_out, not_271_out,
       not_272_out, not_273_out, not_274_out, not_275_out, not_276_out, not_277_out, not_278_out,
       not_279_out, not_280_out, not_281_out, not_282_out, not_283_out, not_284_out, not_285_out,
       not_286_out, not_287_out, not_288_out, not_289_out, not_290_out, not_291_out, not_292_out,
       not_293_out, not_294_out, not_295_out, not_296_out, not_297_out, not_298_out, not_299_out,
       not_300_out, not_301_out, not_302_out, not_303_out, not_304_out, not_305_out, not_306_out,
       not_307_out, not_308_out, not_309_out, not_310_out, not_311_out, not_312_out, not_313_out,
       not_314_out, not_315_out, not_316_out, not_317_out, not_318_out, not_319_out, not_320_out,
       not_321_out, not_322_out, not_323_out, not_324_out, not_325_out, not_326_out, not_327_out,
       not_328_out, not_329_out, not_330_out, not_331_out, not_332_out, not_333_out, not_334_out,
       not_335_out, not_336_out, not_337_out, not_338_out, not_339_out, not_340_out, not_341_out,
       not_342_out, not_343_out, not_344_out, not_345_out, not_346_out, not_347_out, not_348_out,
       not_349_out, not_350_out, not_351_out, not_352_out, not_353_out, not_354_out, not_355_out,
       not_356_out, not_357_out, not_358_out, not_359_out, not_360_out, not_361_out, sal, salx;

  Multiplexer multiplexer_1 (.in0(F0), .in1(1'b0), .out(multiplexer_1_out), .sel(sal));  // open: en
  not not_1 (not_1_out, F5);
  not not_2 (not_2_out, F4);
  not not_3 (not_3_out, F3);
  not not_4 (not_4_out, F2);
  not not_5 (not_5_out, multiplexer_2_out);
  not not_6 (not_6_out, multiplexer_1_out);
  not not_7 (not_7_out, OP4);
  not not_8 (not_8_out, OP2);
  not not_9 (not_9_out, F5);
  not not_10 (not_10_out, F2);
  not not_11 (not_11_out, multiplexer_2_out);
  not not_12 (not_12_out, multiplexer_1_out);
  not not_13 (not_13_out, OP5);
  not not_14 (not_14_out, OP4);
  not not_15 (not_15_out, OP3);
  not not_16 (not_16_out, OP2);
  not not_17 (not_17_out, OP1);
  not not_18 (not_18_out, OP0);
  not not_19 (not_19_out, F4);
  not not_20 (not_20_out, F3);
  not not_21 (not_21_out, F2);
  not not_22 (not_22_out, multiplexer_1_out);
  not not_23 (not_23_out, OP5);
  not not_24 (not_24_out, OP4);
  not not_25 (not_25_out, OP3);
  not not_26 (not_26_out, OP2);
  not not_27 (not_27_out, OP1);
  not not_28 (not_28_out, OP0);
  not not_29 (not_29_out, F4);
  not not_30 (not_30_out, F3);
  not not_31 (not_31_out, multiplexer_2_out);
  not not_32 (not_32_out, OP5);
  not not_33 (not_33_out, OP4);
  not not_34 (not_34_out, OP3);
  not not_35 (not_35_out, OP2);
  not not_36 (not_36_out, OP1);
  not not_37 (not_37_out, OP0);
  not not_38 (not_38_out, F5);
  not not_39 (not_39_out, F4);
  not not_40 (not_40_out, F3);
  not not_41 (not_41_out, F2);
  not not_42 (not_42_out, multiplexer_2_out);
  not not_43 (not_43_out, multiplexer_1_out);
  not not_44 (not_44_out, OP5);
  not not_45 (not_45_out, OP4);
  not not_46 (not_46_out, OP3);
  not not_47 (not_47_out, OP2);
  not not_48 (not_48_out, OP0);
  not not_49 (not_49_out, F5);
  not not_50 (not_50_out, F4);
  not not_51 (not_51_out, F3);
  not not_52 (not_52_out, F2);
  not not_53 (not_53_out, multiplexer_2_out);
  not not_54 (not_54_out, multiplexer_1_out);
  not not_55 (not_55_out, OP5);
  not not_56 (not_56_out, OP4);
  not not_57 (not_57_out, OP2);
  not not_58 (not_58_out, OP1);
  not not_59 (not_59_out, OP0);
  not not_60 (not_60_out, F4);
  not not_61 (not_61_out, F3);
  not not_62 (not_62_out, multiplexer_2_out);
  not not_63 (not_63_out, multiplexer_1_out);
  not not_64 (not_64_out, OP5);
  not not_65 (not_65_out, OP4);
  not not_66 (not_66_out, OP3);
  not not_67 (not_67_out, OP2);
  not not_68 (not_68_out, OP1);
  not not_69 (not_69_out, OP0);
  not not_70 (not_70_out, F4);
  not not_71 (not_71_out, F3);
  not not_72 (not_72_out, multiplexer_2_out);
  not not_73 (not_73_out, OP5);
  not not_74 (not_74_out, OP4);
  not not_75 (not_75_out, OP3);
  not not_76 (not_76_out, OP2);
  not not_77 (not_77_out, OP1);
  not not_78 (not_78_out, OP0);
  not not_79 (not_79_out, F5);
  not not_80 (not_80_out, F4);
  not not_81 (not_81_out, F3);
  not not_82 (not_82_out, F2);
  not not_83 (not_83_out, multiplexer_2_out);
  not not_84 (not_84_out, multiplexer_1_out);
  not not_85 (not_85_out, OP5);
  not not_86 (not_86_out, OP4);
  not not_87 (not_87_out, OP3);
  not not_88 (not_88_out, OP2);
  not not_89 (not_89_out, OP0);
  not not_90 (not_90_out, F5);
  not not_91 (not_91_out, F4);
  not not_92 (not_92_out, F3);
  not not_93 (not_93_out, F2);
  not not_94 (not_94_out, multiplexer_2_out);
  not not_95 (not_95_out, multiplexer_1_out);
  not not_96 (not_96_out, OP5);
  not not_97 (not_97_out, OP4);
  not not_98 (not_98_out, OP3);
  not not_99 (not_99_out, OP1);
  not not_100 (not_100_out, OP0);
  not not_101 (not_101_out, F5);
  not not_102 (not_102_out, F4);
  not not_103 (not_103_out, F3);
  not not_104 (not_104_out, F2);
  not not_105 (not_105_out, multiplexer_2_out);
  not not_106 (not_106_out, multiplexer_1_out);
  not not_107 (not_107_out, OP5);
  not not_108 (not_108_out, OP4);
  not not_109 (not_109_out, OP2);
  not not_110 (not_110_out, OP1);
  not not_111 (not_111_out, OP0);
  not not_112 (not_112_out, F4);
  not not_113 (not_113_out, F3);
  not not_114 (not_114_out, F2);
  not not_115 (not_115_out, multiplexer_1_out);
  not not_116 (not_116_out, OP5);
  not not_117 (not_117_out, OP4);
  not not_118 (not_118_out, OP3);
  not not_119 (not_119_out, OP2);
  not not_120 (not_120_out, OP1);
  not not_121 (not_121_out, OP0);
  not not_122 (not_122_out, F4);
  not not_123 (not_123_out, F3);
  not not_124 (not_124_out, multiplexer_2_out);
  not not_125 (not_125_out, OP5);
  not not_126 (not_126_out, OP4);
  not not_127 (not_127_out, OP3);
  not not_128 (not_128_out, OP2);
  not not_129 (not_129_out, OP1);
  not not_130 (not_130_out, OP0);
  not not_131 (not_131_out, F5);
  not not_132 (not_132_out, F4);
  not not_133 (not_133_out, F3);
  not not_134 (not_134_out, F2);
  not not_135 (not_135_out, multiplexer_2_out);
  not not_136 (not_136_out, multiplexer_1_out);
  not not_137 (not_137_out, OP5);
  not not_138 (not_138_out, OP4);
  not not_139 (not_139_out, OP3);
  not not_140 (not_140_out, OP2);
  not not_141 (not_141_out, OP0);
  not not_142 (not_142_out, F5);
  not not_143 (not_143_out, F4);
  not not_144 (not_144_out, F3);
  not not_145 (not_145_out, F2);
  not not_146 (not_146_out, multiplexer_2_out);
  not not_147 (not_147_out, multiplexer_1_out);
  not not_148 (not_148_out, OP5);
  not not_149 (not_149_out, OP4);
  not not_150 (not_150_out, OP3);
  not not_151 (not_151_out, OP1);
  not not_152 (not_152_out, OP0);
  not not_153 (not_153_out, F5);
  not not_154 (not_154_out, F4);
  not not_155 (not_155_out, F3);
  not not_156 (not_156_out, F2);
  not not_157 (not_157_out, multiplexer_2_out);
  not not_158 (not_158_out, multiplexer_1_out);
  not not_159 (not_159_out, OP5);
  not not_160 (not_160_out, OP4);
  not not_161 (not_161_out, OP2);
  not not_162 (not_162_out, OP1);
  not not_163 (not_163_out, OP0);
  not not_164 (not_164_out, F5);
  not not_165 (not_165_out, F4);
  not not_166 (not_166_out, F3);
  not not_167 (not_167_out, F2);
  not not_168 (not_168_out, multiplexer_2_out);
  not not_169 (not_169_out, multiplexer_1_out);
  not not_170 (not_170_out, OP4);
  not not_171 (not_171_out, OP3);
  not not_172 (not_172_out, OP2);
  not not_173 (not_173_out, F5);
  not not_174 (not_174_out, F2);
  not not_175 (not_175_out, multiplexer_2_out);
  not not_176 (not_176_out, multiplexer_1_out);
  not not_177 (not_177_out, OP5);
  not not_178 (not_178_out, OP4);
  not not_179 (not_179_out, OP3);
  not not_180 (not_180_out, OP2);
  not not_181 (not_181_out, OP1);
  not not_182 (not_182_out, OP0);
  not not_183 (not_183_out, F4);
  not not_184 (not_184_out, F3);
  not not_185 (not_185_out, F2);
  not not_186 (not_186_out, multiplexer_1_out);
  not not_187 (not_187_out, OP5);
  not not_188 (not_188_out, OP4);
  not not_189 (not_189_out, OP3);
  not not_190 (not_190_out, OP2);
  not not_191 (not_191_out, OP1);
  not not_192 (not_192_out, OP0);
  not not_193 (not_193_out, F4);
  not not_194 (not_194_out, F3);
  not not_195 (not_195_out, multiplexer_2_out);
  not not_196 (not_196_out, OP5);
  not not_197 (not_197_out, OP4);
  not not_198 (not_198_out, OP3);
  not not_199 (not_199_out, OP2);
  not not_200 (not_200_out, OP1);
  not not_201 (not_201_out, OP0);
  not not_202 (not_202_out, F5);
  not not_203 (not_203_out, F4);
  not not_204 (not_204_out, F3);
  not not_205 (not_205_out, F2);
  not not_206 (not_206_out, multiplexer_2_out);
  not not_207 (not_207_out, multiplexer_1_out);
  not not_208 (not_208_out, OP5);
  not not_209 (not_209_out, OP4);
  not not_210 (not_210_out, OP3);
  not not_211 (not_211_out, OP2);
  not not_212 (not_212_out, OP0);
  not not_213 (not_213_out, F5);
  not not_214 (not_214_out, F4);
  not not_215 (not_215_out, F3);
  not not_216 (not_216_out, F2);
  not not_217 (not_217_out, multiplexer_2_out);
  not not_218 (not_218_out, multiplexer_1_out);
  not not_219 (not_219_out, OP5);
  not not_220 (not_220_out, OP4);
  not not_221 (not_221_out, OP3);
  not not_222 (not_222_out, OP1);
  not not_223 (not_223_out, OP0);
  not not_224 (not_224_out, F5);
  not not_225 (not_225_out, F4);
  not not_226 (not_226_out, F3);
  not not_227 (not_227_out, F2);
  not not_228 (not_228_out, multiplexer_2_out);
  not not_229 (not_229_out, multiplexer_1_out);
  not not_230 (not_230_out, OP5);
  not not_231 (not_231_out, OP4);
  not not_232 (not_232_out, OP2);
  not not_233 (not_233_out, OP1);
  not not_234 (not_234_out, OP0);
  not not_235 (not_235_out, F5);
  not not_236 (not_236_out, F4);
  not not_237 (not_237_out, F3);
  not not_238 (not_238_out, F2);
  not not_239 (not_239_out, multiplexer_2_out);
  not not_240 (not_240_out, multiplexer_1_out);
  not not_241 (not_241_out, OP4);
  not not_242 (not_242_out, OP2);
  not not_243 (not_243_out, F5);
  not not_244 (not_244_out, F2);
  not not_245 (not_245_out, multiplexer_2_out);
  not not_246 (not_246_out, multiplexer_1_out);
  not not_247 (not_247_out, OP5);
  not not_248 (not_248_out, OP4);
  not not_249 (not_249_out, OP3);
  not not_250 (not_250_out, OP2);
  not not_251 (not_251_out, OP1);
  not not_252 (not_252_out, OP0);
  not not_253 (not_253_out, F4);
  not not_254 (not_254_out, F3);
  not not_255 (not_255_out, multiplexer_2_out);
  not not_256 (not_256_out, multiplexer_1_out);
  not not_257 (not_257_out, OP5);
  not not_258 (not_258_out, OP4);
  not not_259 (not_259_out, OP3);
  not not_260 (not_260_out, OP2);
  not not_261 (not_261_out, OP1);
  not not_262 (not_262_out, OP0);
  not not_263 (not_263_out, F4);
  not not_264 (not_264_out, F3);
  not not_265 (not_265_out, multiplexer_2_out);
  not not_266 (not_266_out, OP5);
  not not_267 (not_267_out, OP4);
  not not_268 (not_268_out, OP3);
  not not_269 (not_269_out, OP2);
  not not_270 (not_270_out, OP1);
  not not_271 (not_271_out, OP0);
  not not_272 (not_272_out, F5);
  not not_273 (not_273_out, F4);
  not not_274 (not_274_out, F3);
  not not_275 (not_275_out, F2);
  not not_276 (not_276_out, multiplexer_2_out);
  not not_277 (not_277_out, multiplexer_1_out);
  not not_278 (not_278_out, OP5);
  not not_279 (not_279_out, OP4);
  not not_280 (not_280_out, OP3);
  not not_281 (not_281_out, OP1);
  not not_282 (not_282_out, OP0);
  not not_283 (not_283_out, F5);
  not not_284 (not_284_out, F4);
  not not_285 (not_285_out, F3);
  not not_286 (not_286_out, F2);
  not not_287 (not_287_out, multiplexer_2_out);
  not not_288 (not_288_out, multiplexer_1_out);
  not not_289 (not_289_out, OP4);
  not not_290 (not_290_out, OP2);
  not not_291 (not_291_out, F5);
  not not_292 (not_292_out, F2);
  not not_293 (not_293_out, multiplexer_2_out);
  not not_294 (not_294_out, multiplexer_1_out);
  not not_295 (not_295_out, OP5);
  not not_296 (not_296_out, OP4);
  not not_297 (not_297_out, OP3);
  not not_298 (not_298_out, OP2);
  not not_299 (not_299_out, OP1);
  not not_300 (not_300_out, OP0);
  not not_301 (not_301_out, F4);
  not not_302 (not_302_out, F3);
  not not_303 (not_303_out, F2);
  not not_304 (not_304_out, multiplexer_1_out);
  not not_305 (not_305_out, OP5);
  not not_306 (not_306_out, OP4);
  not not_307 (not_307_out, OP3);
  not not_308 (not_308_out, OP2);
  not not_309 (not_309_out, OP1);
  not not_310 (not_310_out, OP0);
  not not_311 (not_311_out, F4);
  not not_312 (not_312_out, F3);
  not not_313 (not_313_out, multiplexer_2_out);
  not not_314 (not_314_out, OP5);
  not not_315 (not_315_out, OP4);
  not not_316 (not_316_out, OP3);
  not not_317 (not_317_out, OP2);
  not not_318 (not_318_out, OP1);
  not not_319 (not_319_out, OP0);
  not not_320 (not_320_out, F5);
  not not_321 (not_321_out, F4);
  not not_322 (not_322_out, F3);
  not not_323 (not_323_out, F2);
  not not_324 (not_324_out, multiplexer_2_out);
  not not_325 (not_325_out, multiplexer_1_out);
  not not_326 (not_326_out, OP5);
  not not_327 (not_327_out, OP4);
  not not_328 (not_328_out, OP3);
  not not_329 (not_329_out, OP1);
  not not_330 (not_330_out, OP0);
  not not_331 (not_331_out, F5);
  not not_332 (not_332_out, F4);
  not not_333 (not_333_out, F3);
  not not_334 (not_334_out, F2);
  not not_335 (not_335_out, multiplexer_2_out);
  not not_336 (not_336_out, multiplexer_1_out);
  not not_337 (not_337_out, OP5);
  not not_338 (not_338_out, OP4);
  not not_339 (not_339_out, OP2);
  not not_340 (not_340_out, OP1);
  not not_341 (not_341_out, OP0);
  not not_342 (not_342_out, F5);
  not not_343 (not_343_out, F2);
  not not_344 (not_344_out, multiplexer_2_out);
  not not_345 (not_345_out, multiplexer_1_out);
  not not_346 (not_346_out, OP5);
  not not_347 (not_347_out, OP4);
  not not_348 (not_348_out, OP3);
  not not_349 (not_349_out, OP2);
  not not_350 (not_350_out, OP1);
  not not_351 (not_351_out, OP0);
  not not_352 (not_352_out, F4);
  not not_353 (not_353_out, F3);
  not not_354 (not_354_out, F2);
  not not_355 (not_355_out, multiplexer_1_out);
  not not_356 (not_356_out, OP5);
  not not_357 (not_357_out, OP4);
  not not_358 (not_358_out, OP3);
  not not_359 (not_359_out, OP2);
  not not_360 (not_360_out, OP1);
  not not_361 (not_361_out, OP0);
  and and_1 (and_1_out, not_1_out, not_2_out, not_3_out, not_4_out, not_5_out, not_6_out, OP5, not_7_out, OP3, not_8_out, OP1, OP0);
  and and_2 (and_2_out, not_9_out, F4, F3, not_10_out, not_11_out, not_12_out, not_13_out, not_14_out, not_15_out, not_16_out, not_17_out, not_18_out);
  and and_3 (and_3_out, F5, not_19_out, not_20_out, not_21_out, not_22_out, not_23_out, not_24_out, not_25_out, not_26_out, not_27_out, not_28_out);
  and and_4 (and_4_out, F5, not_29_out, not_30_out, F2, not_31_out, not_32_out, not_33_out, not_34_out, not_35_out, not_36_out, not_37_out);
  and and_5 (and_5_out, not_38_out, not_39_out, not_40_out, not_41_out, not_42_out, not_43_out, not_44_out, not_45_out, not_46_out, not_47_out, OP1, not_48_out);
  and and_6 (and_6_out, not_49_out, not_50_out, not_51_out, not_52_out, not_53_out, not_54_out, not_55_out, not_56_out, OP3, not_57_out, not_58_out, not_59_out);
  and and_7 (and_7_out, F5, not_60_out, not_61_out, not_62_out, not_63_out, not_64_out, not_65_out, not_66_out, not_67_out, not_68_out, not_69_out);
  and and_8 (and_8_out, F5, not_70_out, not_71_out, F2, not_72_out, not_73_out, not_74_out, not_75_out, not_76_out, not_77_out, not_78_out);
  and and_9 (and_9_out, not_79_out, not_80_out, not_81_out, not_82_out, not_83_out, not_84_out, not_85_out, not_86_out, not_87_out, not_88_out, OP1, not_89_out);
  and and_10 (and_10_out, not_90_out, not_91_out, not_92_out, not_93_out, not_94_out, not_95_out, not_96_out, not_97_out, not_98_out, OP2, not_99_out, not_100_out);
  and and_11 (and_11_out, not_101_out, not_102_out, not_103_out, not_104_out, not_105_out, not_106_out, not_107_out, not_108_out, OP3, not_109_out, not_110_out, not_111_out);
  and and_12 (and_12_out, F5, not_112_out, not_113_out, not_114_out, not_115_out, not_116_out, not_117_out, not_118_out, not_119_out, not_120_out, not_121_out);
  and and_13 (and_13_out, F5, not_122_out, not_123_out, F2, not_124_out, not_125_out, not_126_out, not_127_out, not_128_out, not_129_out, not_130_out);
  and and_14 (and_14_out, not_131_out, not_132_out, not_133_out, not_134_out, not_135_out, not_136_out, not_137_out, not_138_out, not_139_out, not_140_out, OP1, not_141_out);
  and and_15 (and_15_out, not_142_out, not_143_out, not_144_out, not_145_out, not_146_out, not_147_out, not_148_out, not_149_out, not_150_out, OP2, not_151_out, not_152_out);
  and and_16 (and_16_out, not_153_out, not_154_out, not_155_out, not_156_out, not_157_out, not_158_out, not_159_out, not_160_out, OP3, not_161_out, not_162_out, not_163_out);
  and and_17 (and_17_out, not_164_out, not_165_out, not_166_out, not_167_out, not_168_out, not_169_out, OP5, not_170_out, not_171_out, not_172_out, OP1, OP0);
  and and_18 (and_18_out, not_173_out, F4, F3, not_174_out, not_175_out, not_176_out, not_177_out, not_178_out, not_179_out, not_180_out, not_181_out, not_182_out);
  and and_19 (and_19_out, F5, not_183_out, not_184_out, not_185_out, multiplexer_2_out, not_186_out, not_187_out, not_188_out, not_189_out, not_190_out, not_191_out, not_192_out);
  and and_20 (and_20_out, F5, not_193_out, not_194_out, F2, not_195_out, multiplexer_1_out, not_196_out, not_197_out, not_198_out, not_199_out, not_200_out, not_201_out);
  and and_21 (and_21_out, not_202_out, not_203_out, not_204_out, not_205_out, not_206_out, not_207_out, not_208_out, not_209_out, not_210_out, not_211_out, OP1, not_212_out);
  and and_22 (and_22_out, not_213_out, not_214_out, not_215_out, not_216_out, not_217_out, not_218_out, not_219_out, not_220_out, not_221_out, OP2, not_222_out, not_223_out);
  and and_23 (and_23_out, not_224_out, not_225_out, not_226_out, not_227_out, not_228_out, not_229_out, not_230_out, not_231_out, OP3, not_232_out, not_233_out, not_234_out);
  and and_24 (and_24_out, not_235_out, not_236_out, not_237_out, not_238_out, not_239_out, not_240_out, OP5, not_241_out, not_242_out, OP1, OP0);
  and and_25 (and_25_out, not_243_out, F4, F3, not_244_out, not_245_out, not_246_out, not_247_out, not_248_out, not_249_out, not_250_out, not_251_out, not_252_out);
  and and_26 (and_26_out, F5, not_253_out, not_254_out, not_255_out, not_256_out, not_257_out, not_258_out, not_259_out, not_260_out, not_261_out, not_262_out);
  and and_27 (and_27_out, F5, not_263_out, not_264_out, F2, not_265_out, not_266_out, not_267_out, not_268_out, not_269_out, not_270_out, not_271_out);
  and and_28 (and_28_out, not_272_out, not_273_out, not_274_out, not_275_out, not_276_out, not_277_out, not_278_out, not_279_out, not_280_out, OP2, not_281_out, not_282_out);
  and and_29 (and_29_out, not_283_out, not_284_out, not_285_out, not_286_out, not_287_out, not_288_out, OP5, not_289_out, not_290_out, OP1, OP0);
  and and_30 (and_30_out, not_291_out, F4, F3, not_292_out, not_293_out, not_294_out, not_295_out, not_296_out, not_297_out, not_298_out, not_299_out, not_300_out);
  and and_31 (and_31_out, F5, not_301_out, not_302_out, not_303_out, not_304_out, not_305_out, not_306_out, not_307_out, not_308_out, not_309_out, not_310_out);
  and and_32 (and_32_out, F5, not_311_out, not_312_out, F2, not_313_out, not_314_out, not_315_out, not_316_out, not_317_out, not_318_out, not_319_out);
  and and_33 (and_33_out, not_320_out, not_321_out, not_322_out, not_323_out, not_324_out, not_325_out, not_326_out, not_327_out, not_328_out, OP2, not_329_out, not_330_out);
  and and_34 (and_34_out, not_331_out, not_332_out, not_333_out, not_334_out, not_335_out, not_336_out, not_337_out, not_338_out, OP3, not_339_out, not_340_out, not_341_out);
  and and_35 (and_35_out, not_342_out, F4, F3, not_343_out, not_344_out, not_345_out, not_346_out, not_347_out, not_348_out, not_349_out, not_350_out, not_351_out);
  and and_36 (and_36_out, F5, not_352_out, not_353_out, not_354_out, not_355_out, not_356_out, not_357_out, not_358_out, not_359_out, not_360_out, not_361_out);
  or or_1 (S0, and_1_out, and_2_out, and_3_out, and_4_out);
  or or_2 (S1, and_5_out, and_6_out, and_7_out, and_8_out);
  or or_3 (S2, and_9_out, and_10_out, and_11_out, and_12_out, and_13_out);
  or or_4 (S3, and_14_out, and_15_out, and_16_out, and_17_out, and_18_out, and_19_out, and_20_out);
  or or_5 (S4, and_21_out, and_22_out, and_23_out, and_24_out, and_25_out, and_26_out, and_27_out);
  or or_6 (S5, and_28_out, and_29_out, and_30_out, and_31_out, and_32_out);
  or or_7 (S6, and_33_out, and_34_out, and_35_out, and_36_out);
  Multiplexer multiplexer_2 (.in0(F1), .in1(1'b0), .out(multiplexer_2_out), .sel(salx));  // open: en
  Comparator #(.width(10)) comparator_1 (
    .a({10{1'b0}}), .b({OP5, OP4, OP2, OP1, OP0, F5, F4, F3, F2, F1}), .eq(comparator_1_eq));  // open: gt, lt
  Comparator #(.width(9)) comparator_2 (
    .a({9{1'b0}}), .b({OP4, OP2, OP1, OP0, F5, F4, F3, F2, OP5}), .eq(comparator_2_eq));  // open: gt, lt
  and and_37 (sal, F0, comparator_1_eq, OP3);
  and and_38 (salx, F1, comparator_2_eq, OP3);

  // Other names for the same wires on the sheet: _2 = F1; _12 = OP5; _3 = F2; _4 = F3; _5 = F4; _6 = F5; _7 = OP0;
  //   _8 = OP1; _9 = OP2; _11 = OP4; _1 = F0; _10 = OP3
endmodule

module control_unit (
  input  op5,
  input  op4,
  input  op3,
  input  op2,
  input  op1,
  input  op0,
  output regDst,
  output aluSrc,
  output memToReg,
  output regWrite,
  output memRead,
  output memWrite,
  output branch,
  output aluOp1,
  output aluOp0,
  output jump
);

  wire and_2_out, and_3_out, and_5_out, and_6_out, not_1_out, not_2_out, not_3_out, not_4_out, not_5_out,
       not_6_out, not_7_out, not_8_out, not_9_out, not_10_out, not_11_out, not_12_out, not_13_out,
       not_14_out, not_15_out, not_16_out, not_17_out, not_18_out, not_19_out, not_20_out, not_21_out,
       not_22_out, not_23_out, not_24_out, not_25_out, not_26_out, not_27_out, not_28_out, not_29_out,
       not_30_out, not_31_out, not_32_out, not_33_out, not_34_out, not_35_out, not_36_out, not_37_out,
       not_38_out, not_39_out, not_40_out, not_41_out, not_42_out, not_43_out, not_44_out, not_45_out,
       not_46_out, not_47_out, not_48_out, not_49_out;

  not not_1 (not_1_out, op5);
  not not_2 (not_2_out, op4);
  not not_3 (not_3_out, op3);
  not not_4 (not_4_out, op1);
  not not_5 (not_5_out, op0);
  not not_6 (not_6_out, op5);
  not not_7 (not_7_out, op4);
  not not_8 (not_8_out, op2);
  not not_9 (not_9_out, op1);
  not not_10 (not_10_out, op0);
  not not_11 (not_11_out, op4);
  not not_12 (not_12_out, op2);
  not not_13 (not_13_out, op4);
  not not_14 (not_14_out, op3);
  not not_15 (not_15_out, op2);
  not not_16 (not_16_out, op5);
  not not_17 (not_17_out, op4);
  not not_18 (not_18_out, op2);
  not not_19 (not_19_out, op1);
  not not_20 (not_20_out, op0);
  not not_21 (not_21_out, op4);
  not not_22 (not_22_out, op3);
  not not_23 (not_23_out, op2);
  not not_24 (not_24_out, op4);
  not not_25 (not_25_out, op3);
  not not_26 (not_26_out, op2);
  not not_27 (not_27_out, op4);
  not not_28 (not_28_out, op2);
  not not_29 (not_29_out, op5);
  not not_30 (not_30_out, op4);
  not not_31 (not_31_out, op3);
  not not_32 (not_32_out, op1);
  not not_33 (not_33_out, op0);
  not not_34 (not_34_out, op5);
  not not_35 (not_35_out, op4);
  not not_36 (not_36_out, op3);
  not not_37 (not_37_out, op2);
  not not_38 (not_38_out, op1);
  not not_39 (not_39_out, op0);
  not not_40 (not_40_out, op5);
  not not_41 (not_41_out, op4);
  not not_42 (not_42_out, op3);
  not not_43 (not_43_out, op1);
  not not_44 (not_44_out, op0);
  not not_45 (not_45_out, op5);
  not not_46 (not_46_out, op4);
  not not_47 (not_47_out, op3);
  not not_48 (not_48_out, op2);
  not not_49 (not_49_out, op0);
  and and_1 (regDst, not_1_out, not_2_out, not_3_out, not_4_out, not_5_out);
  and and_2 (and_2_out, not_6_out, not_7_out, op3, not_8_out, not_9_out, not_10_out);
  and and_3 (and_3_out, op5, not_11_out, not_12_out, op1, op0);
  // AND_Gate and_4 has open pins: in0=op5, in1=not_13_out, in2=not_14_out, in3=not_15_out, in4=op1, in5=op0, out=open
  and and_5 (and_5_out, not_16_out, not_17_out, not_18_out, not_19_out, not_20_out);
  and and_6 (and_6_out, op5, not_21_out, not_22_out, not_23_out, op1, op0);
  and and_7 (memRead, op5, not_24_out, not_25_out, not_26_out, op1, op0);
  and and_8 (memWrite, op5, not_27_out, op3, not_28_out, op1, op0);
  and and_9 (branch, not_29_out, not_30_out, not_31_out, op2, not_32_out, not_33_out);
  and and_10 (aluOp1, not_34_out, not_35_out, not_36_out, not_37_out, not_38_out, not_39_out);
  and and_11 (aluOp0, not_40_out, not_41_out, not_42_out, op2, not_43_out, not_44_out);
  and and_12 (jump, not_45_out, not_46_out, not_47_out, not_48_out, op1, not_49_out);
  or or_1 (aluSrc, and_2_out, and_3_out);
  or or_2 (regWrite, and_5_out, and_6_out);

  assign memToReg = op1;
endmodule

module control_sign_ALU (
  input  aluOp1,
  input  aluOp0,
  input  f5,
  input  f4,
  input  f3,
  input  f2,
  input  f1,
  input  f0,
  output oper3,
  output oper2,
  output oper1,
  output oper0
);

  wire and_1_out, and_2_out, and_3_out, and_4_out, and_5_out, and_6_out, and_7_out, and_8_out, and_9_out,
       and_10_out, and_11_out, and_12_out, and_13_out, and_14_out, and_15_out, and_16_out, and_17_out,
       and_18_out, and_19_out, and_20_out, and_21_out, and_22_out, not_1_out, not_2_out, not_3_out,
       not_4_out, not_5_out, not_6_out, not_7_out, not_8_out, not_9_out, not_10_out, not_11_out, not_12_out,
       not_13_out, not_14_out, not_15_out, not_16_out, not_17_out, not_18_out, not_19_out, not_20_out,
       not_21_out, not_22_out, not_23_out;

  not not_1 (not_1_out, aluOp1);
  not not_2 (not_2_out, aluOp0);
  not not_3 (not_3_out, f3);
  not not_4 (not_4_out, f2);
  not not_5 (not_5_out, f0);
  not not_6 (not_6_out, aluOp0);
  not not_7 (not_7_out, f5);
  not not_8 (not_8_out, f4);
  not not_9 (not_9_out, f3);
  not not_10 (not_10_out, f2);
  not not_11 (not_11_out, f2);
  not not_12 (not_12_out, f1);
  not not_13 (not_13_out, aluOp1);
  and and_1 (and_1_out, not_13_out, aluOp0);
  and and_2 (and_2_out, aluOp0, f1);
  not not_14 (not_14_out, f2);
  and and_3 (and_3_out, aluOp1, not_14_out, f0);
  and and_4 (and_4_out, aluOp1, f2, f1);
  and and_5 (and_5_out, aluOp1, f3);
  and and_6 (and_6_out, aluOp1, f4, f1);
  and and_7 (and_7_out, aluOp1, f5, f1);
  not not_15 (not_15_out, aluOp1);
  not not_16 (not_16_out, f2);
  and and_8 (and_8_out, not_16_out, f0);
  and and_9 (and_9_out, f2, f1);
  and and_10 (and_10_out, f4, not_17_out);
  not not_17 (not_17_out, f2);
  and and_11 (and_11_out, f5, not_18_out);
  not not_18 (not_18_out, f2);
  and and_12 (and_12_out, aluOp0, not_19_out);
  not not_19 (not_19_out, f2);
  not not_20 (not_20_out, aluOp0);
  not not_21 (not_21_out, aluOp0);
  not not_22 (not_22_out, f5);
  not not_23 (not_23_out, f4);
  and and_13 (and_13_out, not_1_out, not_2_out, f5, f4, not_3_out, not_4_out, f1, not_5_out);
  and and_14 (and_14_out, aluOp1, not_6_out, not_7_out, not_8_out, not_9_out, not_10_out);
  and and_15 (and_15_out, aluOp1, not_11_out, f0);
  and and_16 (and_16_out, aluOp1, f2, f1);
  and and_17 (and_17_out, aluOp1, f3, not_12_out);
  and and_18 (and_18_out, not_20_out, f5, f4, f3, f2);
  and and_19 (and_19_out, aluOp1, f0);
  and and_20 (and_20_out, aluOp1, not_21_out, not_22_out, not_23_out, f1);
  and and_21 (and_21_out, aluOp1, f2, f1);
  and and_22 (and_22_out, aluOp1, f3);
  or or_1 (oper3, and_13_out, and_14_out, and_15_out, and_16_out, and_17_out);
  or or_2 (oper2, and_1_out, and_2_out, and_3_out, and_4_out, and_5_out, and_6_out, and_7_out);
  or or_3 (oper1, not_15_out, and_8_out, and_9_out, f3, and_10_out, and_11_out, and_12_out);
  or or_4 (oper0, and_18_out, and_19_out, and_20_out, and_21_out, and_22_out);
endmodule

module ALU (
  input  [31:0] A,
  input  [31:0] B,
  input  [3:0] operation,
  output zero,
  output [31:0] R
);

  wire comparator_1_lt;
  wire [4:0] bit_extender_1_out;
  wire [31:0] adder_1_out, and_1_out, bit_extender_2_out, nor_1_out, or_1_out, shifter_1_out, shifter_2_out,
       subtractor_1_out;

  Bit_Extender #(.in_width(32), .out_width(5)) bit_extender_1 (.in(B), .out(bit_extender_1_out));
  assign and_1_out = A & B;  // AND_Gate and_1, 32 bits wide
  assign or_1_out = A | B;  // OR_Gate or_1, 32 bits wide
  Adder #(.width(32)) adder_1 (.a(A), .b(B), .out(adder_1_out));  // open: cin, cout
  Subtractor #(.width(32)) subtractor_1 (.a(A), .b(B), .out(subtractor_1_out));  // open: bin, bout
  Comparator #(.width(32)) comparator_1 (.a(A), .b(B), .lt(comparator_1_lt));  // open: gt, eq
  assign nor_1_out = ~(A | B);  // NOR_Gate nor_1, 32 bits wide
  Shifter #(.width(32)) shifter_1 (.in(A), .\dist (bit_extender_1_out), .out(shifter_1_out));
  Shifter #(.width(32), .shift("lr")) shifter_2 (.in(A), .\dist (bit_extender_1_out), .out(shifter_2_out));
  assign bit_extender_2_out = {{31{1'b0}}, comparator_1_lt};  // Bit_Extender bit_extender_2
  Comparator #(.width(32)) comparator_2 (.a(subtractor_1_out), .b({32{1'b0}}), .eq(zero));  // open: gt, lt
  Multiplexer #(.select(4), .width(32)) multiplexer_1 (
    .in0(and_1_out), .in1(or_1_out), .in2(adder_1_out), .in6(subtractor_1_out), .in7(bit_extender_2_out),
    .in8(shifter_1_out), .in9(shifter_2_out), .in12(nor_1_out), .out(R), .sel(operation));  // open: in3, in4, in5, in10, in11, in13, in14, in15, en

  // Notes on the sheet:
  //    OPERACIONES ALU
  //    OP_ALU        Operación
  //   0000          AND
  //   0001         OR
  //   0010         ADD
  //    0110         SUB
  //    1100         NOR
  //   1111         INDEFINIDA
  //    1000        SLL
  //    1001        SRL
  //    0111         SET ON LESS THAN
endmodule

module ValidateAddi (
  input  [31:0] Rt,
  input  [15:0] Imm,
  input  ALUSrc,
  output [31:0] Rb
);

  wire [31:0] bit_extender_1_out;

  assign bit_extender_1_out = {{16{1'b0}}, Imm};  // Bit_Extender bit_extender_1
  Multiplexer #(.width(32), .enable("false")) multiplexer_1 (
    .in0(Rt), .in1(bit_extender_1_out), .out(Rb), .sel(ALUSrc));
endmodule

module Memory (
  input  [31:0] Data_In,
  input  [31:0] Address,
  input  Enable,
  input  Clock,
  input  Store,
  output [31:0] Data_Out
);

  wire not_1_out;
  wire [23:0] bit_extender_1_out;

  Bit_Extender #(.in_width(32), .out_width(24)) bit_extender_1 (.in(Address), .out(bit_extender_1_out));
  assign Data_Out = Store ? Data_In : 32'bz;  // Controlled_Buffer controlled_buffer_1
  not not_1 (not_1_out, Store);
  RAM #(.addrWidth(24), .dataWidth(32)) ram_1 (
    .addr(bit_extender_1_out), .data(Data_Out), .sel(Enable), .clk(Clock), .ld(not_1_out));  // open: clr
endmodule

module PC_Change (
  input  [23:0] PC,
  input  [15:0] Offset,
  input  Branch,
  input  Zero,
  input  Jump_Control,
  input  [25:0] Target_Jump,
  output [23:0] PC_Out
);

  wire and_1_out;
  wire [23:0] adder_1_out, adder_2_out, bit_extender_2_out, bit_extender_3_out, multiplexer_1_out,
       multiplexer_2_out, subtractor_1_out;
  wire [27:0] bit_extender_1_out;

  assign bit_extender_1_out = {{2{1'b0}}, Target_Jump};  // Bit_Extender bit_extender_1
  Adder #(.width(24)) adder_1 (.a(PC), .b(24'h1), .out(adder_1_out));  // open: cin, cout
  Bit_Extender #(.in_width(32), .out_width(24)) bit_extender_2 (
    .in({adder_1_out[23:20], bit_extender_1_out}), .out(bit_extender_2_out));
  assign bit_extender_3_out = {{9{1'b0}}, Offset[14:0]};  // Bit_Extender bit_extender_3
  Adder #(.width(24)) adder_2 (.a(adder_1_out), .b(bit_extender_3_out), .out(adder_2_out));  // open: cin, cout
  Subtractor #(.width(24)) subtractor_1 (
    .a(adder_1_out), .b(bit_extender_3_out), .out(subtractor_1_out));  // open: bin, bout
  Multiplexer #(.width(24), .enable("false")) multiplexer_1 (
    .in0(adder_2_out), .in1(subtractor_1_out), .out(multiplexer_1_out), .sel(Offset[15]));
  and and_1 (and_1_out, Branch, Zero);
  Multiplexer #(.width(24), .enable("false")) multiplexer_2 (
    .in0(adder_1_out), .in1(multiplexer_1_out), .out(multiplexer_2_out), .sel(and_1_out));
  Multiplexer #(.width(24), .enable("false")) multiplexer_3 (
    .in0(multiplexer_2_out), .in1(bit_extender_2_out), .out(PC_Out), .sel(Jump_Control));
endmodule

module PIPELINE (
  input  RESET,
  input  RELOJ,
  input  [5:0] OP,
  input  [4:0] RS,
  input  [4:0] RT,
  input  [4:0] RD,
  input  [15:0] IMM,
  input  [4:0] SHAMT,
  input  [5:0] FUNCT,
  input  RegDest,
  input  AluSrc,
  input  Mem2Reg,
  input  RegWrite,
  input  MemRead,
  input  MemWrite,
  input  Branch,
  input  AluOp1,
  input  AluOp0,
  input  Jump,
  input  [31:0] MemReg,
  input  [31:0] BusA,
  input  [31:0] BusB,
  input  [31:0] AluReg,
  input  [4:0] RegDest_2,
  input  [31:0] X,
  input  [23:0] PC,
  input  ENABLE,
  output [5:0] OPA,
  output [4:0] RSA,
  output [4:0] RTA,
  output [4:0] RDA,
  output [15:0] IMMA,
  output [4:0] SHAMTA,
  output [5:0] FUNCTA,
  output RegDestA,
  output AluSrcA,
  output MemReg2,
  output RegWriteA,
  output MedReadA,
  output MemWrite2,
  output BranchA,
  output AluOp1A,
  output AluOp0A,
  output JumpA,
  output [31:0] MemRegA,
  output [31:0] BusAA,
  output [31:0] BusBA,
  output [31:0] AluRegA,
  output [4:0] RegDestA_2,
  output [31:0] XA,
  output [23:0] PCA
);

  wire comparator_1_eq, counter_1_q, multiplexer_1_out;

  Register #(.width(6)) register_1 (.D(OP), .en(ENABLE), .Q(OPA), .clk(RELOJ), .clr(RESET));
  Register #(.width(5)) register_2 (.D(RS), .en(ENABLE), .Q(RSA), .clk(RELOJ), .clr(RESET));
  Register #(.width(5)) register_3 (.D(RT), .en(ENABLE), .Q(RTA), .clk(RELOJ), .clr(RESET));
  Register #(.width(5)) register_4 (.D(RD), .en(ENABLE), .Q(RDA), .clk(RELOJ), .clr(RESET));
  Register #(.width(16)) register_5 (.D(IMM), .en(ENABLE), .Q(IMMA), .clk(RELOJ), .clr(RESET));
  Register #(.width(5)) register_6 (.D(SHAMT), .en(ENABLE), .Q(SHAMTA), .clk(RELOJ), .clr(RESET));
  Register #(.width(6)) register_7 (.D(FUNCT), .en(ENABLE), .Q(FUNCTA), .clk(RELOJ), .clr(RESET));
  Register #(.width(1)) register_8 (.D(RegDest), .en(ENABLE), .Q(RegDestA), .clk(RELOJ), .clr(RESET));
  Register #(.width(1)) register_9 (.D(AluSrc), .en(ENABLE), .Q(AluSrcA), .clk(RELOJ), .clr(RESET));
  Register #(.width(1)) register_10 (.D(Mem2Reg), .en(ENABLE), .Q(MemReg2), .clk(RELOJ), .clr(RESET));
  Register #(.width(1)) register_11 (.D(RegWrite), .en(ENABLE), .Q(RegWriteA), .clk(RELOJ), .clr(RESET));
  Register #(.width(1)) register_12 (.D(MemRead), .en(ENABLE), .Q(MedReadA), .clk(RELOJ), .clr(RESET));
  Register #(.width(1)) register_13 (.D(MemWrite), .en(ENABLE), .Q(MemWrite2), .clk(RELOJ), .clr(RESET));
  Register #(.width(1)) register_14 (.D(Branch), .en(ENABLE), .Q(BranchA), .clk(RELOJ), .clr(RESET));
  Register #(.width(1)) register_15 (.D(AluOp1), .en(ENABLE), .Q(AluOp1A), .clk(RELOJ), .clr(RESET));
  Register #(.width(1)) register_16 (.D(AluOp0), .en(ENABLE), .Q(AluOp0A), .clk(RELOJ), .clr(RESET));
  Register #(.width(1)) register_17 (.D(Jump), .en(ENABLE), .Q(JumpA), .clk(RELOJ), .clr(RESET));
  Register #(.width(32)) register_18 (.D(MemReg), .en(ENABLE), .Q(MemRegA), .clk(RELOJ), .clr(RESET));
  Register #(.width(32)) register_19 (.D(BusA), .en(ENABLE), .Q(BusAA), .clk(RELOJ), .clr(RESET));
  Register #(.width(32)) register_20 (.D(BusB), .en(ENABLE), .Q(BusBA), .clk(RELOJ), .clr(RESET));
  Register #(.width(32)) register_21 (.D(AluReg), .en(ENABLE), .Q(AluRegA), .clk(RELOJ), .clr(RESET));
  Register #(.width(5)) register_22 (.D(RegDest_2), .en(ENABLE), .Q(RegDestA_2), .clk(RELOJ), .clr(RESET));
  Register #(.width(32)) register_23 (.D(X), .en(ENABLE), .Q(XA), .clk(RELOJ), .clr(RESET));
  Register #(.width(24)) register_24 (.D(PC), .en(ENABLE), .Q(PCA), .clk(RELOJ), .clr(RESET));
  Multiplexer multiplexer_1 (.in0(comparator_1_eq), .in1(RESET), .out(multiplexer_1_out), .sel(ENABLE));  // open: en
  Counter #(.width(1), .max('h1)) counter_1 (
    .D(1'b1), .Q(counter_1_q), .clk(RELOJ), .clr(ENABLE));  // open: load, count, carry
  Comparator #(.width(1)) comparator_1 (.a(1'b1), .b(counter_1_q), .eq(comparator_1_eq));  // open: gt, lt

  // Other names for the same wires on the sheet: RES = RESET
endmodule

module HAZ (
  input  [4:0] in_1,
  input  in_2,
  input  RegWrite__1,
  input  [4:0] RD__0,
  input  [4:0] in_5,
  input  [4:0] RD__RT,
  output out_7,
  output [1:0] out_8,
  output [1:0] out_9
);

  wire and_1_out, Check, comparator_1_eq, comparator_2_eq, comparator_3_eq, comparator_4_eq, comparator_5_eq,
       comparator_6_eq, comparator_7_eq, EN, not_1_out, not_4_out, not_5_out, not_6_out, or_1_out;

  Comparator #(.width(5)) comparator_1 (.a(RD__0), .b({5{1'b0}}), .eq(comparator_1_eq));  // open: gt, lt
  not not_1 (not_1_out, comparator_1_eq);
  Comparator #(.width(5)) comparator_2 (.a(RD__0), .b(in_5), .eq(comparator_2_eq));  // open: gt, lt
  Comparator #(.width(5)) comparator_3 (.a(RD__0), .b(RD__RT), .eq(comparator_3_eq));  // open: gt, lt
  and and_1 (and_1_out, RegWrite__1, not_1_out);
  and and_2 (out_8[1], and_1_out, comparator_2_eq);
  LED led_1 (.in(out_8[1]));
  and and_3 (out_9[1], comparator_3_eq, and_1_out);
  LED led_2 (.in(out_9[1]));
  not not_2 (Check, out_7);
  not not_3 (out_7, or_1_out);
  or or_1 (or_1_out, out_8[1], out_9[1]);
  Multiplexer multiplexer_1 (.in0(Check), .in1(out_7), .out(EN), .sel(out_7));  // open: en
  Comparator #(.width(5)) comparator_4 (.a(in_1), .b({5{1'b0}}), .eq(comparator_4_eq));  // open: gt, lt
  Comparator #(.width(5)) comparator_5 (.a(in_5), .b(RD__0), .eq(comparator_5_eq));  // open: gt, lt
  Comparator #(.width(5)) comparator_6 (.a(in_1), .b(in_5), .eq(comparator_6_eq));  // open: gt, lt
  Comparator #(.width(5)) comparator_7 (.a(in_1), .b(RD__RT), .eq(comparator_7_eq));  // open: gt, lt
  not not_4 (not_4_out, comparator_4_eq);
  not not_5 (not_5_out, comparator_5_eq);
  not not_6 (not_6_out, comparator_3_eq);
  and and_4 (out_8[0], in_2, not_4_out, not_5_out, comparator_6_eq);
  LED led_3 (.in(out_8[0]));
  and and_5 (out_9[0], in_2, not_4_out, not_6_out, comparator_7_eq);
  LED led_4 (.in(out_9[0]));

  // Other names for the same wires on the sheet: ENABLE = out_7

  // Notes on the sheet:
  //    RD==RS
  //    EXE HAZARD
  //    ForwadA=10
  //    ForwadB=10
  //    RegWrite==1
  //    RD <> 0
  //    RD <> RS
  //    RD == RS
endmodule

module PIPELINE1 (
  input  RESET,
  input  RELOJ,
  input  [5:0] OP,
  input  [4:0] RS,
  input  [4:0] RT,
  input  [4:0] RD,
  input  [15:0] IMM,
  input  [4:0] SHAMT,
  input  [5:0] FUNCT,
  input  RegDest,
  input  AluSrc,
  input  Mem2Reg,
  input  RegWrite,
  input  MemRead,
  input  MemWrite,
  input  Branch,
  input  AluOp1,
  input  AluOp0,
  input  Jump,
  input  [31:0] MemReg,
  input  [31:0] BusA,
  input  [31:0] BusB,
  input  [31:0] AluReg,
  input  [4:0] RegDest_2,
  input  [31:0] X,
  input  [23:0] PC,
  input  ENABLE,
  output [5:0] OPA,
  output [4:0] RSA,
  output [4:0] RTA,
  output [4:0] RDA,
  output [15:0] IMMA,
  output [4:0] SHAMTA,
  output [5:0] FUNCTA,
  output RegDestA,
  output AluSrcA,
  output MemReg2,
  output RegWriteA,
  output MedReadA,
  output MemWrite2,
  output BranchA,
  output AluOp1A,
  output AluOp0A,
  output JumpA,
  output [31:0] MemRegA,
  output [31:0] BusAA,
  output [31:0] BusBA,
  output [31:0] AluRegA,
  output [4:0] RegDestA_2,
  output [31:0] XA,
  output [23:0] PCA
);

  wire comparator_1_eq, counter_1_q, multiplexer_1_out;

  Register #(.width(6)) register_1 (.D(OP), .en(ENABLE), .Q(OPA), .clk(RELOJ), .clr(RESET));
  Register #(.width(5)) register_2 (.D(RS), .en(ENABLE), .Q(RSA), .clk(RELOJ), .clr(RESET));
  Register #(.width(5)) register_3 (.D(RT), .en(ENABLE), .Q(RTA), .clk(RELOJ), .clr(RESET));
  Register #(.width(5)) register_4 (.D(RD), .en(ENABLE), .Q(RDA), .clk(RELOJ), .clr(RESET));
  Register #(.width(16)) register_5 (.D(IMM), .en(ENABLE), .Q(IMMA), .clk(RELOJ), .clr(RESET));
  Register #(.width(5)) register_6 (.D(SHAMT), .en(ENABLE), .Q(SHAMTA), .clk(RELOJ), .clr(RESET));
  Register #(.width(6)) register_7 (.D(FUNCT), .en(ENABLE), .Q(FUNCTA), .clk(RELOJ), .clr(RESET));
  Register #(.width(1)) register_8 (.D(RegDest), .en(ENABLE), .Q(RegDestA), .clk(RELOJ), .clr(RESET));
  Register #(.width(1)) register_9 (.D(AluSrc), .en(ENABLE), .Q(AluSrcA), .clk(RELOJ), .clr(RESET));
  Register #(.width(1)) register_10 (.D(Mem2Reg), .en(ENABLE), .Q(MemReg2), .clk(RELOJ), .clr(RESET));
  Register #(.width(1)) register_11 (.D(RegWrite), .en(ENABLE), .Q(RegWriteA), .clk(RELOJ), .clr(RESET));
  Register #(.width(1)) register_12 (.D(MemRead), .en(ENABLE), .Q(MedReadA), .clk(RELOJ), .clr(RESET));
  Register #(.width(1)) register_13 (.D(MemWrite), .en(ENABLE), .Q(MemWrite2), .clk(RELOJ), .clr(RESET));
  Register #(.width(1)) register_14 (.D(Branch), .en(ENABLE), .Q(BranchA), .clk(RELOJ), .clr(RESET));
  Register #(.width(1)) register_15 (.D(AluOp1), .en(ENABLE), .Q(AluOp1A), .clk(RELOJ), .clr(RESET));
  Register #(.width(1)) register_16 (.D(AluOp0), .en(ENABLE), .Q(AluOp0A), .clk(RELOJ), .clr(RESET));
  Register #(.width(1)) register_17 (.D(Jump), .en(ENABLE), .Q(JumpA), .clk(RELOJ), .clr(RESET));
  Register #(.width(32)) register_18 (.D(MemReg), .en(ENABLE), .Q(MemRegA), .clk(RELOJ), .clr(RESET));
  Register #(.width(32)) register_19 (.D(BusA), .en(ENABLE), .Q(BusAA), .clk(RELOJ), .clr(RESET));
  Register #(.width(32)) register_20 (.D(BusB), .en(ENABLE), .Q(BusBA), .clk(RELOJ), .clr(RESET));
  Register #(.width(32)) register_21 (.D(AluReg), .en(ENABLE), .Q(AluRegA), .clk(RELOJ), .clr(RESET));
  Register #(.width(5)) register_22 (.D(RegDest_2), .en(ENABLE), .Q(RegDestA_2), .clk(RELOJ), .clr(RESET));
  Register #(.width(32)) register_23 (.D(X), .en(ENABLE), .Q(XA), .clk(RELOJ), .clr(RESET));
  Register #(.width(24)) register_24 (.D(PC), .en(ENABLE), .Q(PCA), .clk(RELOJ), .clr(RESET));
  Multiplexer multiplexer_1 (.in0(comparator_1_eq), .in1(RESET), .out(multiplexer_1_out), .sel(ENABLE));  // open: en
  Counter #(.width(1), .max('h1)) counter_1 (
    .D(1'b1), .Q(counter_1_q), .clk(RELOJ), .clr(ENABLE));  // open: load, count, carry
  Comparator #(.width(1)) comparator_1 (.a(1'b1), .b(counter_1_q), .eq(comparator_1_eq));  // open: gt, lt

  // Other names for the same wires on the sheet: RES = RESET
endmodule

module HazardUnitLS (
  input  ID_EX_MemRead,
  input  [4:0] ID_EX_RegisterRT,
  input  [4:0] IF_ID_RegisterRS,
  input  [4:0] IF_ID_RegisterRT,
  output out_5
);

  wire comparator_1_eq, comparator_2_eq, or_1_out;

  Comparator #(.width(5)) comparator_1 (
    .a(ID_EX_RegisterRT), .b(IF_ID_RegisterRS), .eq(comparator_1_eq));  // open: gt, lt
  Comparator #(.width(5)) comparator_2 (
    .a(ID_EX_RegisterRT), .b(IF_ID_RegisterRT), .eq(comparator_2_eq));  // open: gt, lt
  or or_1 (or_1_out, comparator_1_eq, comparator_2_eq);
  and and_1 (out_5, ID_EX_MemRead, or_1_out);
endmodule
